# Fritzing sketch smartswitch (saved by Fritzing 0.9.2b)
breadboards: 1

parts:
  Part1 = Spark Core (v1.0)
  KY-1 = Keyes Relay [package=THT]
  DHT1 = DHT22 Humidity and Temperature Sensor

nets:
  GND: Part1.GND, KY-1.ground, DHT1.GND
  N1: Part1.D2, DHT1.DATA
  N2: Part1.D6, KY-1.signal
  N3: Part1.3V3*, KY-1.power, DHT1.VDD

custom parts:
  Keyes Relay: The Keyes 5V relay module is suitable for SCM development, home appliance control. It uses a 5V~12V TIL control signal which can control DC / AC signal.
